// Logisim project music_player_circuits.circ as structural Verilog: 1 circuit, main circuit asm1
module asm1 (
  input  in_1,
  input  in_2,
  input  in_3
);

  wire and_1_out, and_2_out, and_3_out, and_4_out, and_5_out, and_7_out, and_8_out, and_9_out, and_10_out,
       and_11_out, and_12_out, and_13_out, and_14_out, and_15_out, and_16_out, and_18_out, and_19_out,
       and_20_out, and_21_out, and_22_out, and_23_out, and_24_out, and_25_out, and_26_out, and_28_out,
       and_29_out, and_30_out, and_31_out, and_32_out, and_33_out, and_34_out, and_35_out, and_36_out,
       and_38_out, and_39_out, and_40_out, and_41_out, and_42_out, and_44_out, and_45_out, and_46_out,
       and_47_out, and_49_out, and_50_out, and_51_out, and_53_out, and_54_out, and_55_out, button_1_out,
       button_2_out, button_3_out, button_4_out, button_5_out, button_6_out, button_7_out, button_8_out,
       button_9_out, d_ff_1_q, d_ff_2_qn, d_ff_3_qn, d_ff_4_q, d_ff_5_q, d_ff_6_q, d_ff_7_q, d_ff_8_q,
       d_ff_9_q, d_ff_10_q, d_ff_11_q, j_k_ff_1_q, j_k_ff_1_qn, j_k_ff_2_q, j_k_ff_2_qn, j_k_ff_3_q,
       j_k_ff_3_qn, j_k_ff_4_q, j_k_ff_4_qn, j_k_ff_5_q, j_k_ff_5_qn, j_k_ff_6_q, j_k_ff_6_qn, j_k_ff_7_q,
       j_k_ff_7_qn, j_k_ff_8_q, j_k_ff_8_qn, nor_1_out, nor_2_out, not_1_out, not_2_out, not_3_out,
       not_4_out, not_5_out, not_6_out, or_1_out, or_2_out, or_3_out, or_4_out, or_5_out, or_6_out, or_7_out,
       or_8_out, or_9_out, or_10_out, or_11_out, or_12_out, or_13_out, or_14_out, t_ff_1_q, t_ff_1_qn,
       t_ff_2_q, t_ff_2_qn, t_ff_3_q, t_ff_3_qn, xor_1_out, xor_2_out, xor_3_out;
  wire [3:0] and_6_out, and_43_out;

  Button button_1 (.out(button_1_out));
  Button button_2 (.out(button_2_out));
  not not_1 (not_1_out, button_2_out);
  Button button_3 (.out(button_3_out));
  Button button_4 (.out(button_4_out));
  Button button_5 (.out(button_5_out));
  xor xor_1 (xor_1_out, button_1_out, not_1_out);
  D_Flip_Flop d_ff_1 (.D(button_3_out), .clk(button_3_out), .Q(d_ff_1_q), .reset(button_4_out));  // open: Qn, preset
  T_Flip_Flop t_ff_1 (.T(button_5_out), .clk(button_5_out), .Q(t_ff_1_q), .Qn(t_ff_1_qn));  // open: reset, preset
  not not_2 (not_2_out, xor_1_out);
  Button button_6 (.out(button_6_out));
  Button button_7 (.out(button_7_out));
  not not_3 (not_3_out, button_7_out);
  and and_1 (and_1_out, d_ff_1_q, t_ff_1_q);
  and and_2 (and_2_out, d_ff_1_q, t_ff_1_qn);
  xor xor_2 (xor_2_out, button_6_out, not_3_out);
  not not_4 (not_4_out, xor_2_out);
  D_Flip_Flop d_ff_2 (.D(button_1_out), .clk(not_2_out), .Qn(d_ff_2_qn));  // open: Q, preset, reset
  LED led_1 (.in(and_1_out));
  LED led_2 (.in(and_2_out));
  D_Flip_Flop d_ff_3 (.D(button_2_out), .clk(not_2_out), .Qn(d_ff_3_qn));  // open: Q, preset, reset
  and and_3 (and_3_out, button_6_out, button_6_out);
  and and_4 (and_4_out, button_7_out, d_ff_5_q);
  or or_1 (or_1_out, and_3_out, and_4_out);
  D_Flip_Flop d_ff_4 (.D(or_1_out), .clk(not_4_out), .Q(d_ff_4_q), .reset(in_1));  // open: Qn, preset
  J_K_Flip_Flop j_k_ff_1 (
    .J(not_2_out), .K(not_2_out), .clk(not_2_out), .Q(j_k_ff_1_q), .Qn(j_k_ff_1_qn));  // open: preset, reset
  and and_5 (and_5_out, d_ff_4_q, d_ff_1_q);
  and and_6 (and_6_out[0], j_k_ff_1_q, d_ff_1_q);
  and and_7 (and_7_out, d_ff_4_q, button_6_out);
  or or_2 (or_2_out, and_7_out, and_8_out);
  D_Flip_Flop d_ff_5 (.D(or_2_out), .clk(not_4_out), .Q(d_ff_5_q), .reset(in_1));  // open: Qn, preset
  Button button_8 (.out(button_8_out));
  Button button_9 (.out(button_9_out));
  and and_8 (and_8_out, button_7_out, d_ff_6_q);
  and and_9 (and_9_out, d_ff_5_q, button_6_out);
  and and_10 (and_10_out, d_ff_5_q, d_ff_1_q);
  and and_11 (and_11_out, j_k_ff_4_q, j_k_ff_1_qn, button_2_out);
  and and_12 (and_12_out, j_k_ff_4_qn, j_k_ff_1_q, button_1_out);
  and and_13 (and_13_out, j_k_ff_2_q, j_k_ff_1_qn, button_2_out);
  and and_14 (and_14_out, j_k_ff_3_q, j_k_ff_1_qn, button_2_out);
  T_Flip_Flop t_ff_2 (
    .T(button_8_out), .clk(button_8_out), .Q(t_ff_2_q), .Qn(t_ff_2_qn), .reset(t_ff_3_qn));  // open: preset
  T_Flip_Flop t_ff_3 (.T(button_9_out), .clk(button_9_out), .Q(t_ff_3_q), .Qn(t_ff_3_qn));  // open: reset, preset
  or or_3 (or_3_out, and_9_out, and_15_out);
  D_Flip_Flop d_ff_6 (.D(or_3_out), .clk(not_4_out), .Q(d_ff_6_q), .reset(in_1));  // open: Qn, preset
  and and_15 (and_15_out, button_7_out, d_ff_7_q);
  and and_16 (and_16_out, d_ff_6_q, d_ff_1_q);
  or or_4 (or_4_out, and_11_out, and_12_out, and_13_out, and_14_out);
  J_K_Flip_Flop j_k_ff_2 (
    .J(or_4_out), .K(or_4_out), .clk(not_2_out), .Q(j_k_ff_2_q), .Qn(j_k_ff_2_qn));  // open: preset, reset
  and and_17 (and_6_out[1], j_k_ff_2_q, d_ff_1_q);
  and and_18 (and_18_out, t_ff_2_qn, t_ff_3_q);
  and and_19 (and_19_out, t_ff_2_q, t_ff_3_q);
  and and_20 (and_20_out, d_ff_6_q, button_6_out);
  or or_5 (or_5_out, and_20_out, and_21_out);
  and and_21 (and_21_out, button_7_out, d_ff_8_q);
  D_Flip_Flop d_ff_7 (.D(or_5_out), .clk(not_4_out), .Q(d_ff_7_q), .reset(in_1));  // open: Qn, preset
  and and_22 (and_22_out, j_k_ff_3_q, j_k_ff_2_qn, j_k_ff_1_qn, button_2_out);
  and and_23 (and_23_out, j_k_ff_4_q, j_k_ff_1_qn, button_2_out);
  and and_24 (and_24_out, j_k_ff_2_q, j_k_ff_1_q, button_1_out);
  LED led_3 (.in(and_18_out));
  LED led_4 (.in(and_19_out));
  and and_25 (and_25_out, d_ff_7_q, d_ff_1_q);
  and and_26 (and_26_out, d_ff_7_q, button_6_out);
  LedBar ledbar_1 (
    .led0(and_5_out), .led1(and_10_out), .led2(and_16_out), .led3(and_25_out), .led4(and_29_out),
    .led5(and_35_out), .led6(and_39_out), .led7(and_42_out));
  or or_6 (or_6_out, and_22_out, and_23_out, and_24_out);
  J_K_Flip_Flop j_k_ff_3 (
    .J(or_6_out), .K(or_6_out), .clk(not_2_out), .Q(j_k_ff_3_q), .Qn(j_k_ff_3_qn));  // open: preset, reset
  or or_7 (or_7_out, and_26_out, and_28_out);
  D_Flip_Flop d_ff_8 (.D(or_7_out), .clk(not_4_out), .Q(d_ff_8_q), .reset(in_1));  // open: Qn, preset
  and and_27 (and_6_out[2], j_k_ff_3_q, d_ff_1_q);
  and and_28 (and_28_out, button_7_out, d_ff_9_q);
  and and_29 (and_29_out, d_ff_8_q, d_ff_1_q);
  and and_30 (and_30_out, d_ff_8_q, button_6_out);
  or or_8 (or_8_out, and_30_out, and_34_out);
  and and_31 (and_31_out, j_k_ff_3_qn, j_k_ff_2_qn, button_2_out, j_k_ff_1_qn);
  and and_32 (and_32_out, j_k_ff_4_q, j_k_ff_1_q, button_1_out);
  and and_33 (and_33_out, j_k_ff_3_q, j_k_ff_2_q, j_k_ff_1_q, button_1_out);
  and and_34 (and_34_out, button_7_out, d_ff_10_q);
  D_Flip_Flop d_ff_9 (.D(or_8_out), .clk(not_4_out), .Q(d_ff_9_q), .reset(in_1));  // open: Qn, preset
  or or_9 (or_9_out, and_31_out, and_32_out, and_33_out);
  J_K_Flip_Flop j_k_ff_4 (
    .J(or_9_out), .K(or_9_out), .clk(not_2_out), .Q(j_k_ff_4_q), .Qn(j_k_ff_4_qn));  // open: preset, reset
  and and_35 (and_35_out, d_ff_9_q, d_ff_1_q);
  Hex_Digit_Display hex_digit_display_1 (.value(and_43_out));  // open: dp
  Hex_Digit_Display hex_digit_display_2 (.value(and_6_out));  // open: dp
  not not_5 (not_5_out, j_k_ff_1_q);
  and and_36 (and_36_out, d_ff_9_q, button_6_out);
  not not_6 (not_6_out, j_k_ff_4_q);
  and and_37 (and_6_out[3], j_k_ff_4_q, d_ff_1_q);
  and and_38 (and_38_out, button_7_out, d_ff_11_q);
  or or_10 (or_10_out, and_36_out, and_38_out);
  D_Flip_Flop d_ff_10 (.D(or_10_out), .clk(not_4_out), .Q(d_ff_10_q), .reset(in_1));  // open: Qn, preset
  and and_39 (and_39_out, d_ff_10_q, d_ff_1_q);
  and and_40 (and_40_out, d_ff_10_q, button_6_out);
  nor nor_1 (nor_1_out, j_k_ff_1_q, j_k_ff_2_q, j_k_ff_3_q, j_k_ff_4_q, d_ff_2_qn);
  nor nor_2 (nor_2_out, not_5_out, j_k_ff_2_q, j_k_ff_3_q, not_6_out, d_ff_3_qn);
  or or_11 (or_11_out, and_40_out, and_41_out);
  D_Flip_Flop d_ff_11 (.D(or_11_out), .clk(not_4_out), .Q(d_ff_11_q), .reset(in_1));  // open: Qn, preset
  xor xor_3 (xor_3_out, nor_1_out, nor_2_out);
  and and_41 (and_41_out, button_7_out, button_6_out);
  and and_42 (and_42_out, d_ff_11_q, d_ff_1_q);
  J_K_Flip_Flop j_k_ff_5 (
    .J(xor_3_out), .K(xor_3_out), .clk(xor_3_out), .Q(j_k_ff_5_q), .Qn(j_k_ff_5_qn));  // open: preset, reset
  and and_43 (and_43_out[0], j_k_ff_5_q, d_ff_1_q);
  and and_44 (and_44_out, j_k_ff_8_q, j_k_ff_5_qn, button_2_out);
  and and_45 (and_45_out, j_k_ff_8_qn, j_k_ff_5_q, button_1_out);
  and and_46 (and_46_out, j_k_ff_6_q, j_k_ff_5_qn, button_2_out);
  and and_47 (and_47_out, j_k_ff_7_q, j_k_ff_5_qn, button_2_out);
  or or_12 (or_12_out, and_44_out, and_45_out, and_46_out, and_47_out);
  J_K_Flip_Flop j_k_ff_6 (
    .J(or_12_out), .K(or_12_out), .clk(xor_3_out), .Q(j_k_ff_6_q), .Qn(j_k_ff_6_qn));  // open: preset, reset
  and and_48 (and_43_out[1], j_k_ff_6_q, d_ff_1_q);
  and and_49 (and_49_out, j_k_ff_7_q, j_k_ff_6_qn, j_k_ff_5_qn, button_2_out);
  and and_50 (and_50_out, j_k_ff_8_q, j_k_ff_5_qn, button_2_out);
  and and_51 (and_51_out, j_k_ff_6_q, j_k_ff_5_q, button_1_out);
  or or_13 (or_13_out, and_49_out, and_50_out, and_51_out);
  J_K_Flip_Flop j_k_ff_7 (
    .J(or_13_out), .K(or_13_out), .clk(xor_3_out), .Q(j_k_ff_7_q), .Qn(j_k_ff_7_qn));  // open: preset, reset
  and and_52 (and_43_out[2], j_k_ff_7_q, d_ff_1_q);
  and and_53 (and_53_out, j_k_ff_7_qn, j_k_ff_6_qn, button_2_out, j_k_ff_5_qn);
  and and_54 (and_54_out, j_k_ff_8_q, j_k_ff_5_q, button_1_out);
  and and_55 (and_55_out, j_k_ff_7_q, j_k_ff_6_q, j_k_ff_5_q, button_1_out);
  or or_14 (or_14_out, and_53_out, and_54_out, and_55_out);
  J_K_Flip_Flop j_k_ff_8 (
    .J(or_14_out), .K(or_14_out), .clk(xor_3_out), .Q(j_k_ff_8_q), .Qn(j_k_ff_8_qn));  // open: preset, reset
  and and_56 (and_43_out[3], j_k_ff_8_q, d_ff_1_q);

  // Notes on the sheet:
  //   >> NEXT Button
  //   << Previous Button
  //   On Button
  //   Off Button
  //   Play/ Pause Button
  //   Stage 4: ON/OFF + Play/Pause Button
  //   VOL+ Button
  //   VOL- Button
  //   Play led
  //   Pause led
  //   PAUSE Button
  //   PLAY Button
  //   Stage 1: Play  and Pause Button
  //   Stage 2
  //   Play led
  //   Pause led
  //   Stage 3
endmodule
